# Fritzing sketch Sketch (saved by Fritzing 0.9.5d)
breadboards: 1

parts:
  Componente1 = Arduino Uno (Rev3)
  S1 = Momentary Switch [package=ksa_sealed_tac_switch]
  R1 = Resistor [tolerance=±5% resistance=220 package=THT]
  U1 = LM386 [package=dip08]
  SP1 = SPEAKER [package=pcb_mount_speaker]
  R2 = Rotary Potentiometer (Small) [maximum_resistance=100kΩ package=THT]
  C1 = Capacitor Polarized [package=cpol-radial-1000uf-25v]
  R3 = Resistor [tolerance=±5% resistance=220 package=THT]

nets:
  N1: Componente1.D10_PWM/SS, S1.1, R1.Pin_0
  N2: Componente1.D3_PWM, R3.Pin_1
  N3: Componente1.5V, S1.3, U1.+IN
  N4: Componente1.GND, R1.Pin_1, U1.OUT, U1.BP, SP1.+, R2.leg1
  N5: U1.GAIN, R2.wiper, C1.+, C1.-
  N6: U1.V-, SP1.-
  N7: U1.V+, R3.Pin_0
